// Logisim project T2.circ as structural Verilog: 3 circuits, main circuit m0
module main (
  input  [9:0] m_IN,
  input  [5:0] e_IN,
  input  START,
  output [9:0] m_OUT,
  output [5:0] e_OUT,
  output READY
);

  wire clock_1_out;

  Clock clock_1 (.out(clock_1_out));
  NORMA norma_1 (
    .m_IN(m_IN), .e_IN(e_IN), .START(START), .CLOCK(clock_1_out), .m_OUT(m_OUT), .e_OUT(e_OUT), .READY(READY));
endmodule

module m0 (
  input  [9:0] MANTISA_IN,
  output [9:0] MANTISA_OUT,
  output NORMAL
);


  assign MANTISA_OUT = MANTISA_IN;
  assign NORMAL = MANTISA_IN[9];
endmodule

module NORMA (
  input  [9:0] m_IN,
  input  [5:0] e_IN,
  input  START,
  input  CLOCK,
  output [9:0] m_OUT,
  output [5:0] e_OUT,
  output READY
);

  wire [5:0] _4, multiplexer_2_out, subtractor_1_out;
  wire [9:0] _3, multiplexer_1_out, register_1_q, shifter_1_out;

  Multiplexer #(.width(10), .enable("false")) multiplexer_1 (
    .in0(_3), .in1(m_IN), .out(multiplexer_1_out), .sel(START));
  Multiplexer #(.width(6), .enable("false")) multiplexer_2 (.in0(_4), .in1(e_IN), .out(multiplexer_2_out), .sel(START));
  m0 m0_1 (.MANTISA_IN(register_1_q), .NORMAL(READY), .MANTISA_OUT(m_OUT));
  Register #(.width(10), .trigger("falling")) register_1 (
    .D(multiplexer_1_out), .Q(register_1_q), .clk(CLOCK));  // open: en, clr
  Register #(.width(6), .trigger("falling")) register_2 (
    .D(multiplexer_2_out), .Q(e_OUT), .clk(CLOCK));  // open: en, clr
  Shifter #(.width(10)) shifter_1 (.in(m_OUT), .\dist (4'b0001), .out(shifter_1_out));
  Subtractor #(.width(6)) subtractor_1 (.a(e_OUT), .b(6'b000001), .out(subtractor_1_out));  // open: bin, bout
  Multiplexer #(.width(10), .enable("false")) multiplexer_3 (.in0(shifter_1_out), .in1(m_OUT), .out(_3), .sel(READY));
  Multiplexer #(.width(6), .enable("false")) multiplexer_4 (.in0(subtractor_1_out), .in1(e_OUT), .out(_4), .sel(READY));

  // Other names for the same wires on the sheet: _1 = START; _2 = CLOCK
endmodule
